# Fritzing sketch SCENT_wiring (saved by Fritzing 1.0.6)
breadboards: 2

parts:
  Part1 = Adafruit BME680 [part_number="Adafruit #3660"]
  Part2 = Adafruit CCS811 [part_number="Adafruit #3566"]
  Part3 = MQ-9 breakout
  Sensor1 = Gas Sensor Breakout Board
  Part4 = MQ-3 breakout
  Part5 = Adafruit ADS1115 16Bit I2C ADC [part_number="Adafruit #1085"]
  F1 = Fan - Ventilador [package=THT]
  A1 = Raspberry Pi 5
  S1 = Square Pushbutton

nets:
  N1: Part1.SDI/SDA, Part2.SDA, Part5.SDA
  GND: Part1.GND, Part2.GND, Part3.GND, Sensor1.GND, Part4.GND, Part5.GND, F1.GND, A1.GND
  N2: Part1.SCK/SCL, Part2.SCL, Part5.SCL
  VCC: Part1.VCC, Part2.VCC, Part2.!WAKE, Part5.VDD, A1.3V3
  VCC_2: Part3.VCC, Sensor1.5V, Part4.VCC, A1.5V, S1.leg1
  N3: Part3.AO, Part5.AIN1, A1.GPIO5
  N4: Sensor1.AOUT, Part5.AIN0, A1.GPIO6
  N5: Part4.AO, Part5.AIN2, A1.ID_SD
  N6: F1.5V, S1.leg0

custom parts:
  Adafruit CCS811: Breathe easy - we finally have an I2C VOC/eCO2 sensor in the Adafruit shop! Add air quality monitoring to your project and with an Adafruit CCS811 Air Quality Sensor Breakout. This sensor from AMS is a gas sensor that can detect a wide range of Volatile Organic Compounds (VOCs) and is intended for indoor air quality monitoring. When connected to your microcontroller (running our library code)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
  MQ-9 breakout: SKU: 101284
  Gas Sensor Breakout Board: Gas sensor breakout board. Input voltage is 5V. Sensor output is available in analog and digital.
  MQ-3 breakout: Alcohol sensor is capable of detecting alcohol (ethanol) particles on itself and gives the information in digital form back to us to manipulate with it. SKU:101251 • Voltage: 5V DC • Power: max 750mW • Measurement range: 0.04-4mg/L
  Adafruit ADS1115 16Bit I2C ADC: For microcontrollers without an analog-to-digital converter or when you want a higher-precision ADC, the ADS1115 provides 16-bit precision at 860 samples/second over I2C. The chip can be configured as 4 single-ended input channels, or two differential channels. As a nice bonus, it even includes a programmable gain amplifier, up to x16, to help boost up smaller single/differential signals to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
  Fan - Ventilador: Ventilador de 2 pines, se encuentra comunmente en computadoras de escritorio
  Raspberry Pi 5: The RPi5, a faster version of the awesome Raspberry Pi4B ARM Board with 40 pin gpio.
